# Fritzing sketch Emma (saved by Fritzing 0.9.9b)
circuit board: 8.46667cm x 5.64444cm
breadboards: 2

parts:
  U1 = ESP32-38PinWide [part_number=ESP32-38PinWide]
  M1 = MAX30102
  DHT1 = Humidity and Temperature Sensor DHT11
  U2 = GAS_SENSOR [package=mq-3]
  R1 = Resistor [tolerance=±5% power=0.25 resistance=220 package=THT]

nets:
  VCC: U1.3.3, M1.VIN, DHT1.Vcc, U2.VCC
  N1: U1.GPIO34, R1.Pin_0
  N2: U1.GPIO14, M1.SDA
  N3: U1.GND, DHT1.GND_2
  N4: U1.GPIO13, DHT1.Data-signal
  GND: U1.GPIO11, M1.GND, U2.GND
  N5: U1.GPIO15, M1.SCL
  N6: U2.A0, R1.Pin_1

custom parts:
  ESP32-38PinWide: Generic 38-Pin ESP32 with wide format (only access to one side of pins on a breadboard) based on Stephen Lilley's HiLetgo ESP-WROOM-32 ESP32 ESP-32S Development Board.
  MAX30102: Oximeter module using the MAX30102 chip. You may wish to read (and check your module) this post on power problems with these modules: https://reedpaper.wordpress.com/2018/08/22/pulse-oximeter-max30100-max30102-how-to-fix-wrong-board/ . As usual, if you want the mounting holes in pcb, you need to drag a hole over the pad in silkscreen to actually drill the hole (by default they are not drilled)
  Humidity and Temperature Sensor DHT11: Digital relative humidity & temperature sensor DHT11
  GAS_SENSOR: MQ-3 alcohol gas sensor . FP not tested. SEN-08880.
